# Fritzing sketch NamaInstrument_1.0 (saved by Fritzing 0.9.3b)

parts:
  Part9 = LilyPad Accelerometer ADXL335 [part_number=3]
  Part10 = LilyPad Accelerometer ADXL335 [part_number=4]
  Part11 = LilyPad Accelerometer ADXL335 [part_number=2]
  Part12 = LilyPad Accelerometer ADXL335 [part_number=5]
  Part13 = LilyPad Accelerometer ADXL335 [part_number=1]
  Part14 = LilyPad XBee [part_number=0]  # not connected
  Part8 = LilyPad LiPower
  Part15 = Lilypad Arduino Board  # not connected

nets:
  N1: Part9.COM, Part10.COM, Part11.COM, Part12.COM, Part13.COM, Part8.GND
